# Fritzing sketch DoubleClick (saved by Fritzing 0.5.2b)
breadboards: 1

parts:
  LED-Red = Red LED - 5mm [package="5 mm [THT]"]
  LED-Blue = Blue LED - 5mm [package="5 mm [THT]"]
  LED-Yellow = yellow LED - 5mm [package="5 mm [THT]"]
  Arduino1 = Arduino
  S1 = Pushbutton [package="[THT]"]
  R1 = Resistor [resistance=220 package=THT]
  R1_2 = Resistor [resistance=220 package=THT]
  R1_3 = Resistor [resistance=220 package=THT]
  R4 = Resistor [resistance=220 package=THT]
  LED-White = white LED - 5mm [package="5 mm [THT]"]

nets:
  N1: LED-Red.cathode, LED-Blue.cathode, LED-Yellow.cathode, Arduino1.GND, LED-White.cathode
  N2: LED-Red.anode, R1_2.Pin_0
  N3: LED-Blue.anode, R1_3.Pin_0
  N4: LED-Yellow.anode, R1.Pin_0
  N5: Arduino1.D11, R1.Pin_1
  N6: Arduino1.D10, R1_2.Pin_1
  N7: Arduino1.D9, R1_3.Pin_1
  N8: Arduino1.D2, S1.Pin_3, S1.Pin_4, R4.Pin_1
  N9: Arduino1.+5V, S1.Pin_1, S1.Pin_2
  N10: R4.Pin_0, LED-White.anode
