# Fritzing sketch EasyLights (saved by Fritzing 0.8.3b)
breadboards: 2

parts:
  Part1 = Arduino Uno (Rev3)
  Part2 = XBee Explorer Regulated
  U2 = XBee  # not connected
  LED1 = LED - 5mm [color="Yellow (585nm)" package="5 mm [THT]"]
  LED2 = LED - 5mm [color="White (6500K)" package="5 mm [THT]"]
  LED3 = LED - 5mm [color="Infrared (940nm)" package="5 mm [THT]"]
  LED4 = LED - 5mm [color="Blue (430nm)" package="5 mm [THT]"]
  LED5 = LED - 5mm [color="Blue (430nm)" package="5 mm [THT]"]
  LED6 = LED - 5mm [color="Green (555nm)" package="5 mm [THT]"]

nets:
  N1: Part1.ICSP_SCK, Part1.D13/SCK, Part2.DIN
  GND: Part1.GND, Part2.GND, LED1.cathode, LED2.anode, LED3.anode, LED4.anode, LED5.anode, LED6.anode
  5V: Part1.5V, Part2.5V
  N2: Part1.D8, LED6.cathode
  N3: Part1.D9_PWM, LED1.anode
  N4: Part1.D3_PWM, LED2.cathode
  N5: Part1.D4, LED4.cathode
  N6: Part1.D5_PWM, LED5.cathode
  N7: Part1.D7, LED3.cathode
