# Fritzing sketch SmartServos (saved by Fritzing 0.9.3b)
breadboards: 1

parts:
  Part1 = Arduino Mega 2560 (Rev3)
  MOTOR1 = 28BYJ-48 Stepper Motor
  BREAKOUT1 = ULN2003A breakout board
  MOTOR2 = 28BYJ-48 Stepper Motor
  BREAKOUT2 = ULN2003A breakout board
  MOTOR3 = 28BYJ-48 Stepper Motor
  BREAKOUT3 = ULN2003A breakout board
  MOTOR4 = 28BYJ-48 Stepper Motor
  BREAKOUT4 = ULN2003A breakout board

nets:
  +5V: Part1.5V, BREAKOUT1.+5V, BREAKOUT2.+5V, BREAKOUT2.ON/OFF_jumper_switch, BREAKOUT3.+5V, BREAKOUT4.+5V
  N1: Part1.GND, BREAKOUT1.0V, BREAKOUT2.0V, BREAKOUT3.0V, BREAKOUT4.0V
  N2: Part1.D22, BREAKOUT4.In_1
  N3: Part1.D23, BREAKOUT4.In_2
  N4: Part1.D24, BREAKOUT4.In_3
  N5: Part1.D25, BREAKOUT4.In_4
  N6: MOTOR1.RED, BREAKOUT1.RED_wire
  N7: MOTOR1.ORANGE, BREAKOUT1.ORANGE_wire
  N8: MOTOR1.YELLOW, BREAKOUT1.YELLOW_wire
  N9: MOTOR1.PINK, BREAKOUT1.PINK_wire
  N10: MOTOR1.BLUE, BREAKOUT1.BLUE_wire
  N11: MOTOR2.RED, BREAKOUT2.RED_wire
  N12: MOTOR2.ORANGE, BREAKOUT2.ORANGE_wire
  N13: MOTOR2.YELLOW, BREAKOUT2.YELLOW_wire
  N14: MOTOR2.PINK, BREAKOUT2.PINK_wire
  N15: MOTOR2.BLUE, BREAKOUT2.BLUE_wire
  N16: MOTOR3.RED, BREAKOUT3.RED_wire
  N17: MOTOR3.ORANGE, BREAKOUT3.ORANGE_wire
  N18: MOTOR3.YELLOW, BREAKOUT3.YELLOW_wire
  N19: MOTOR3.PINK, BREAKOUT3.PINK_wire
  N20: MOTOR3.BLUE, BREAKOUT3.BLUE_wire
  N21: MOTOR4.RED, BREAKOUT4.RED_wire
  N22: MOTOR4.ORANGE, BREAKOUT4.ORANGE_wire
  N23: MOTOR4.YELLOW, BREAKOUT4.YELLOW_wire
  N24: MOTOR4.PINK, BREAKOUT4.PINK_wire
  N25: MOTOR4.BLUE, BREAKOUT4.BLUE_wire

custom parts:
  ULN2003A breakout board: ULN2003A 7-way Darlington Transistor Driver on breakoutboard
