# Fritzing sketch EasyLights (saved by Fritzing 0.8.5b)
breadboards: 2

parts:
  Part2 = XBee Explorer Regulated
  U2 = XBee  # not connected
  LED1 = LED - 5mm [color="White (4500K)" package="5 mm [THT]"]
  LED2 = LED - 5mm [color="Yellow (585nm)" package="5 mm [THT]"]
  LED3 = LED - 5mm [color="Infrared (940nm)" package="5 mm [THT]"]
  LED4 = LED - 5mm [color="Yellow (585nm)" package="5 mm [THT]"]
  LED5 = LED - 5mm [color="Blue (430nm)" package="5 mm [THT]"]
  LED6 = LED - 5mm [color="Green (555nm)" package="5 mm [THT]"]
  Part1 = Arduino Uno (Rev3)
  LED7 = LED - 5mm [color="Blue (430nm)" package="5 mm [THT]"]
  LED8 = LED - 5mm [color="Green (555nm)" package="5 mm [THT]"]

nets:
  N1: Part2.DIN, Part1.D13/SCK
  N2: Part2.DOUT, Part1.D12/MISO
  5V: Part2.5V, Part1.5V
  GND: Part2.GND, LED1.cathode, LED2.anode, LED3.anode, LED4.anode, LED5.anode, LED6.anode, Part1.GND, LED7.anode, LED8.cathode
  N3: LED1.anode, Part1.D9_PWM
  N4: LED2.cathode, Part1.D3_PWM
  N5: LED3.cathode, Part1.D7
  N6: LED4.cathode, Part1.D5_PWM
  N7: LED5.cathode, Part1.D4
  N8: LED6.cathode, Part1.D8
  N9: Part1.D10_PWM/SS, LED8.anode
  N10: Part1.D6_PWM, LED7.cathode
